// Logisim project countLeadZeros.circ as structural Verilog: 1 circuit, main circuit main
module main (
);

  wire multiplexer_1_out, multiplexer_2_out, multiplexer_3_out, multiplexer_4_out, multiplexer_6_out,
       multiplexer_7_out, or_1_out, or_2_out, or_3_out, or_4_out, or_5_out;
  wire [2:0] multiplexer_5_out, multiplexer_8_out, multiplexer_9_out, multiplexer_10_out, multiplexer_11_out,
       multiplexer_12_out, multiplexer_13_out, or_6_out;

  Multiplexer #(.enable("false")) multiplexer_1 (.in0(1'b0), .in1(1'b0), .out(multiplexer_1_out), .sel(1'b0));
  Multiplexer #(.enable("false")) multiplexer_2 (.in0(1'b0), .in1(1'b0), .out(multiplexer_2_out), .sel(or_2_out));
  Multiplexer #(.enable("false")) multiplexer_3 (.in0(1'b0), .in1(1'b0), .out(multiplexer_3_out), .sel(or_3_out));
  Multiplexer #(.enable("false")) multiplexer_4 (.in0(1'b0), .in1(1'b0), .out(multiplexer_4_out), .sel(or_1_out));
  or or_1 (or_1_out, multiplexer_1_out, 1'b0);
  Multiplexer #(.width(3), .enable("false")) multiplexer_5 (
    .in0(3'b000), .in1(3'b001), .out(multiplexer_5_out), .sel(multiplexer_2_out));
  or or_2 (or_2_out, multiplexer_3_out, or_3_out);
  or or_3 (or_3_out, multiplexer_6_out, or_4_out);
  Multiplexer #(.enable("false")) multiplexer_6 (.in0(1'b1), .in1(1'b0), .out(multiplexer_6_out), .sel(or_4_out));
  or or_4 (or_4_out, multiplexer_7_out, or_5_out);
  Multiplexer #(.enable("false")) multiplexer_7 (.in0(1'b0), .in1(1'b0), .out(multiplexer_7_out), .sel(or_5_out));
  or or_5 (or_5_out, multiplexer_4_out, or_1_out);
  Multiplexer #(.width(3), .enable("false")) multiplexer_8 (
    .in0(3'b000), .in1(3'b010), .out(multiplexer_8_out), .sel(multiplexer_3_out));
  Multiplexer #(.width(3), .enable("false")) multiplexer_9 (
    .in0(3'b000), .in1(3'b011), .out(multiplexer_9_out), .sel(multiplexer_6_out));
  Multiplexer #(.width(3), .enable("false")) multiplexer_10 (
    .in0(3'b000), .in1(3'b100), .out(multiplexer_10_out), .sel(multiplexer_7_out));
  Multiplexer #(.width(3), .enable("false")) multiplexer_11 (
    .in0(3'b000), .in1(3'b101), .out(multiplexer_11_out), .sel(multiplexer_4_out));
  Multiplexer #(.width(3), .enable("false")) multiplexer_12 (
    .in0(3'b000), .in1(3'b110), .out(multiplexer_12_out), .sel(multiplexer_1_out));
  Multiplexer #(.width(3), .enable("false")) multiplexer_13 (
    .in0(3'b000), .in1(3'b111), .out(multiplexer_13_out), .sel(1'b0));
  assign or_6_out = multiplexer_5_out | multiplexer_8_out | multiplexer_9_out | multiplexer_10_out | multiplexer_11_out | multiplexer_12_out | multiplexer_13_out;  // OR_Gate or_6, 3 bits wide

  // Notes on the sheet:
  //   Magnitude (11 bits)
  //   Exponent (3 bits)
  //   or_6 drives only 1 and floats otherwise
endmodule
