// Logisim project rounding.circ as structural Verilog: 1 circuit, main circuit main
module main (
);

  wire adder_1_cout, adder_2_cout;
  wire [2:0] adder_1_out, multiplexer_2_out, multiplexer_3_out;
  wire [3:0] adder_2_out, adder_3_out, multiplexer_1_out, multiplexer_4_out, multiplexer_5_out, shifter_1_out;

  Adder #(.width(3)) adder_1 (.a(3'b111), .b(3'b001), .out(adder_1_out), .cout(adder_1_cout));  // open: cin
  Adder #(.width(4)) adder_2 (.a(4'b1111), .b(4'b0001), .out(adder_2_out), .cout(adder_2_cout));  // open: cin
  Multiplexer #(.width(4), .enable("false")) multiplexer_1 (
    .in0(adder_2_out), .in1(4'b1111), .out(multiplexer_1_out), .sel(1'b1));
  Multiplexer #(.width(3), .enable("false")) multiplexer_2 (
    .in0(3'b111), .in1(adder_1_out), .out(multiplexer_2_out), .sel(adder_2_cout));
  Shifter #(.width(4), .shift("lr")) shifter_1 (.in(4'b1111), .\dist (2'b01), .out(shifter_1_out));
  Adder #(.width(4)) adder_3 (.a(4'b0001), .b(shifter_1_out), .out(adder_3_out));  // open: cin, cout
  Multiplexer #(.width(3), .enable("false")) multiplexer_3 (
    .in0(multiplexer_2_out), .in1(3'b111), .out(multiplexer_3_out), .sel(adder_1_cout));
  Multiplexer #(.width(4), .enable("false")) multiplexer_4 (
    .in0(multiplexer_1_out), .in1(adder_3_out), .out(multiplexer_4_out), .sel(adder_2_cout));
  Multiplexer #(.width(4), .enable("false")) multiplexer_5 (
    .in0(multiplexer_4_out), .in1(4'b1111), .out(multiplexer_5_out), .sel(adder_1_cout));

  // Notes on the sheet:
  //   Exponent
  //   Significand
  //   Fifth bit
  //   Exponent
  //   Significand
endmodule
